// Logisim project 8bit_CPU.circ as structural Verilog: 4 circuits, main circuit main
module main (
);

  wire clock_1_out, not_1_out, not_2_out, por_1_out, tcore_1_rw;
  wire [7:0] controlled_buffer_1_out, multiplexer_1_out, RAM_1_dout, ROM_1_data, tcore_1_data_out;
  wire [14:0] tcore_1_addr;
  wire [15:15] tcore_1_addr_2;

  Clock clock_1 (.out(clock_1_out));
  POR #(.PorHighDuration(1)) por_1 (.out(por_1_out));
  RAM #(.addrWidth(15), .enables("line")) RAM_1 (
    .addr(tcore_1_addr), .we(tcore_1_rw), .clk(clock_1_out), .din(tcore_1_data_out), .dout(RAM_1_dout));
  not not_1 (not_1_out, por_1_out);
  Multiplexer #(.width(8)) multiplexer_1 (
    .in0(RAM_1_dout), .in1(ROM_1_data), .out(multiplexer_1_out), .sel(tcore_1_addr_2[15]));
  assign controlled_buffer_1_out = not_2_out ? multiplexer_1_out : 8'bz;  // Controlled_Buffer controlled_buffer_1
  ROM #(.addrWidth(15)) ROM_1 (.addr(tcore_1_addr), .data(ROM_1_data));
  not not_2 (not_2_out, tcore_1_rw);
  TCORE tcore_1 (
    .DATA_IN(controlled_buffer_1_out), .CLCK(clock_1_out), .RSTb(not_1_out), .DATA_OUT(tcore_1_data_out),
    .RW(tcore_1_rw), .ADDR({tcore_1_addr_2[15], tcore_1_addr}));

  // Notes on the sheet:
  //   contents of ROM_1 (hex, n*v repeats v):
  //   a9 f0 a2 1 85 1 69 2 95 1 32755*0 80 0 80
endmodule

module BCD_ADD8b (
  input  [7:0] INPUT2,
  input  [7:0] INPUT1,
  input  CARRY_IN,
  output [3:0] D0,
  output [3:0] D1,
  output HC,
  output D2
);

  wire adder_1_cout, adder_3_cout, and_1_out, and_2_out, and_3_out, and_4_out;
  wire [3:0] adder_1_out, adder_3_out;
  wire [3:3] pull_resistor_1_node, pull_resistor_2_node;

  or or_1 (D2, adder_1_cout, and_1_out, and_2_out);
  and and_1 (and_1_out, adder_1_out[3], adder_1_out[2]);
  and and_2 (and_2_out, adder_1_out[3], adder_1_out[1]);
  Pull_Resistor pull_resistor_1 (.node(pull_resistor_1_node[3]));
  Adder #(.width(4)) adder_1 (.a(INPUT1[7:4]), .b(INPUT2[7:4]), .out(adder_1_out), .cin(HC), .cout(adder_1_cout));
  Adder #(.width(4)) adder_2 (
    .a(adder_1_out), .b({pull_resistor_1_node[3], {2{D2}}, pull_resistor_1_node[3]}), .out(D1));  // open: cin, cout
  or or_2 (HC, adder_3_cout, and_3_out, and_4_out);
  and and_3 (and_3_out, adder_3_out[3], adder_3_out[2]);
  and and_4 (and_4_out, adder_3_out[3], adder_3_out[1]);
  Pull_Resistor pull_resistor_2 (.node(pull_resistor_2_node[3]));
  Adder #(.width(4)) adder_3 (.a(INPUT1[3:0]), .b(INPUT2[3:0]), .out(adder_3_out), .cin(CARRY_IN), .cout(adder_3_cout));
  Adder #(.width(4)) adder_4 (
    .a(adder_3_out), .b({pull_resistor_2_node[3], {2{HC}}, pull_resistor_2_node[3]}), .out(D0));  // open: cin, cout
endmodule

module ALU8b (
  input  Input_1,
  input  Input_2,
  input  [7:0] Input_bus_1,
  input  Input_3,
  input  Input_4,
  input  Input_5,
  input  Input_6,
  input  in_8,
  input  [7:0] in_9,
  output [7:0] Output_bus_1,
  output Output_1,
  output Output_2,
  output out_13
);

  wire adder_1_cout, and_1_out, and_4_out, and_6_out, and_7_out, and_9_out, BCD_ADD8b_1_d2,
       bitselector_1_out, bitselector_2_out, bitselector_3_out, bitselector_4_out, not_2_out, not_3_out,
       or_1_out, or_5_out, xor_2_out;
  wire [2:0] bit_extender_2_out;
  wire [7:0] adder_1_out, and_2_out, and_3_out, and_5_out, BCD_ADD8b_1_d0, bit_extender_1_out, not_1_out,
       or_2_out, or_3_out, shifter_1_out, xor_1_out;

  and and_1 (and_1_out, Input_3, adder_1_cout);
  assign bit_extender_1_out = {{7{Input_2}}, Input_2};  // Bit_Extender bit_extender_1
  Adder adder_1 (.a(Input_bus_1), .b(in_9), .out(adder_1_out), .cin(Input_1), .cout(adder_1_cout));
  assign and_2_out = adder_1_out & not_1_out;  // AND_Gate and_2, 8 bits wide
  assign not_1_out = ~bit_extender_1_out;  // NOT_Gate not_1, 8 bits wide
  assign and_3_out = bit_extender_1_out & BCD_ADD8b_1_d0;  // AND_Gate and_3, 8 bits wide
  and and_4 (and_4_out, Input_2, BCD_ADD8b_1_d2);
  BCD_ADD8b BCD_ADD8b_1 (
    .INPUT2(Input_bus_1), .INPUT1(in_9), .CARRY_IN(Input_1), .D0(BCD_ADD8b_1_d0[3:0]),
    .D1(BCD_ADD8b_1_d0[7:4]), .HC(Output_1), .D2(BCD_ADD8b_1_d2));
  or or_1 (or_1_out, and_4_out, and_1_out);
  assign or_2_out = and_2_out | and_3_out;  // OR_Gate or_2, 8 bits wide
  assign bit_extender_2_out = {{2{1'b0}}, 1'b1};  // Bit_Extender bit_extender_2
  assign Output_bus_1 = Input_3 ? or_2_out : 8'bz;  // Controlled_Buffer controlled_buffer_1
  assign and_5_out = Input_bus_1 & in_9;  // AND_Gate and_5, 8 bits wide
  assign Output_bus_1 = Input_4 ? and_5_out : 8'bz;  // Controlled_Buffer controlled_buffer_2
  assign xor_1_out = Input_bus_1 ^ in_9;  // XOR_Gate xor_1, 8 bits wide
  assign Output_bus_1 = Input_5 ? xor_1_out : 8'bz;  // Controlled_Buffer controlled_buffer_3
  assign or_3_out = Input_bus_1 | in_9;  // OR_Gate or_3, 8 bits wide
  assign Output_bus_1 = Input_6 ? or_3_out : 8'bz;  // Controlled_Buffer controlled_buffer_4
  assign Output_bus_1 = in_8 ? shifter_1_out : 8'bz;  // Controlled_Buffer controlled_buffer_5
  Shifter #(.shift("lr")) shifter_1 (.in(in_9), .\dist (bit_extender_2_out), .out(shifter_1_out));
  BitSelector bitselector_1 (.in(in_9), .out(bitselector_1_out), .sel(3'b000));
  and and_6 (and_6_out, bitselector_1_out, in_8);
  or or_4 (out_13, or_1_out, and_6_out);
  Pull_Resistor pull_resistor_1 (.node(Output_bus_1));
  BitSelector bitselector_2 (.in(Output_bus_1), .out(bitselector_2_out), .sel(3'b111));
  BitSelector bitselector_3 (.in(Input_bus_1), .out(bitselector_3_out), .sel(3'b111));
  BitSelector bitselector_4 (.in(in_9), .out(bitselector_4_out), .sel(3'b111));
  xor xor_2 (xor_2_out, bitselector_2_out, bitselector_3_out);
  and and_7 (and_7_out, bitselector_3_out, bitselector_4_out);
  not not_2 (not_2_out, bitselector_3_out);
  not not_3 (not_3_out, bitselector_4_out);
  and and_8 (Output_2, xor_2_out, or_5_out);
  or or_5 (or_5_out, and_7_out, and_9_out);
  and and_9 (and_9_out, not_2_out, not_3_out);
  Pull_Resistor pull_resistor_2 ();  // open: node
endmodule

module TCORE (
  input  [7:0] DATA_IN,
  input  CLCK,
  input  RSTb,
  output [7:0] DATA_OUT,
  output RW,
  output [15:0] ADDR
);

  wire AC_DB, AC_SB, ACR, ACR_C, ADD_ADL, ADD_SB06, ADD_SB7, adder_1_cout, ADH_ABH, ADH_PCH, ADL_ABL,
       ADL_ADD, ADL_PCL, and_1_out, ANDS, AVR, AVR_V, B, bitselector_1_out, BRK, BRKHB_ADB, BRKLB_ADB, C,
       CL2, D, DAA, DB0_C, DB1_Z, DB2_I, DB3_D, DB6_V, DB7_N, DB_ADD, DBx_ADD, DBZ_Z, decoder_1_out0,
       decoder_1_out1, decoder_2_out1, decoder_2_out2, decoder_2_out9, decoder_2_out10, DL_ADH, DL_ADL,
       DL_DB, DSA, EORS, HC, I, I_ADDC, I_PC, I_V, IR5_C, IR5_D, IR5_I, N, not_5_out, O_ADD, O_ADH0, O_ADH17,
       O_ADL0, O_ADL1, O_ADL2, or_2_out, or_4_out, or_5_out, or_6_out, or_7_out, or_8_out, or_9_out,
       or_10_out, or_12_out, ORS, P_DB, PCH_ADH, PCH_DB, PCH_PCH, PCL_ADL, PCL_DB, PCL_PCL,
       pull_resistor_2_node, RST, RST_CYCLE, RST_q, RSTHB_ADB, RSTLB_ADB, S_ADL, S_SB, SB_AC, SB_ADD, SB_ADH,
       SB_DB, SB_S, SB_X, SB_Y, SRS, SUMS, V, X_SB, Y_SB, Z;
  wire [1:0] IRQPLA_out, priority_encoder_1_out, priority_encoder_2_out, priority_encoder_3_out,
       priority_encoder_4_out, priority_encoder_5_out;
  wire [2:0] FlagSelect_out, or_11_out;
  wire [5:5] P_q;
  wire [6:0] controlled_buffer_20_out;
  wire [7:0] ABH_q, ABL_q, AC_q, ADD_q, adder_1_out, adder_2_out, AI_q, ALU8b_1_output_bus_1, BI_q,
       bit_extender_1_out, bit_extender_3_out, controlled_buffer_2_out, controlled_buffer_3_out,
       controlled_buffer_6_out, controlled_buffer_9_out, controlled_buffer_13_out, controlled_buffer_22_out,
       controlled_buffer_27_out, DL_q, DOR_q, multiplexer_3_out, not_4_out, or_1_out, PCH_q, PCHS_q, PCL_q,
       PCLS_q, PD_q, S_q, X_q, Y_q;
  wire [7:7] controlled_buffer_21_out;
  wire [12:0] counter_1_q;
  wire [15:0] Vectors_out;
  wire [62:0] and_4_out, and_8_out, bit_extender_2_out, DecodePLA_out, not_3_out, ResetPLA_out;

  Decoder #(.enable("false"), .select(4)) decoder_1 (
    .out0(decoder_1_out0), .out1(decoder_1_out1), .sel(counter_1_q[3:0]));  // open: out2, out3, out4, out5, out6, out7, out8, out9, out10, out11, out12, out13, out14, out15
  assign or_1_out = bit_extender_1_out | counter_1_q[12:5];  // OR_Gate or_1, 8 bits wide
  PLA #(.in_width(8), .\table ("00000000 01")) IRQPLA (.in(or_1_out), .out(IRQPLA_out));
  Register IR (.D(PD_q), .en(decoder_2_out1), .clk(CLCK), .Q(counter_1_q[12:5]), .clr(RST));
  Pull_Resistor pull_resistor_1 (.node(counter_1_q[4]));
  not not_1 (RST, RSTb);
  D_Flip_Flop u_RST (.D(RSTb), .clk(RSTb), .Q(RST_q), .reset(and_1_out));  // open: Qn, preset
  and and_1 (and_1_out, RST_q, RST_CYCLE);
  assign bit_extender_1_out = {{7{RST_q}}, RST_q};  // Bit_Extender bit_extender_1
  Multiplexer #(.select(3)) multiplexer_1 (
    .in0(pull_resistor_2_node), .in1(C), .in2(Z), .in3(I), .in4(D), .in5(B), .in6(V), .in7(N),
    .out(counter_1_q[4]), .sel(FlagSelect_out));
  PLA #(.in_width(13), .out_width(63), .\table ("xxxxxxxxx0000 000000000000000000000000000000000000000000000001000101001100000\nxxxxxxxxx0001 000000000000000000000000000000000000000000000000001000010000000\n0110100100010 000000000000000000000000000000000000000000000001000101001100000\n0110100100011 000010000000100000001001000000001000010000000000001000010000001\n0110100100100 001000000010000000000010011000000000000000000100000000000000000\n0110100100101 100000000000000000000000000000000000000000000000000000000000000\n0110010100010 000000000000000000000000000000000000000000000001000101001100000\n0110010100011 000000000000000000000000000000000000000000000000001000011111010\n0110010100100 000010000000100000001001000000001000010000000000000000000000001\n0110010100101 001000000010000000000010011000000000000000000100000000000000000\n0110010100110 100000000000000000000000000000000000000000000000000000000000000\n0111010100010 000000000000000000000000000000000000000000000001000101001100000\n0111010100011 000000000000000000100001000000001000010000000000001000010111001\n0111010100100 000000000000000000000000000100000000000000000000000000001000000\n0111010100101 000010000000100000001001000000001000010000000000000000000000001\n0111010100110 001000000010000000000010011000000000000000000100000000000000000\n0111010100111 100000000000000000000000000000000000000000000000000000000000000\n0110110100010 000000000000000000000000000000000000000000000001000101001100000\n0110110100011 000000000000000000000000100000001000010000000001001101011100001\n0110110100100 000000000000000000000000000100000000000000000000001000011100100\n0110110100101 000010000000100000001001000000001000010000000000000000000000001\n0110110100110 001000000010000000000010011000000000000000000100000000000000000\n0110110100111 100000000000000000000000000000000000000000000000000000000000000\n01111101x0010 000000000000000000000000000000000000000000000001000101001100000\n01111101x0011 000000000000100000100001000000001000010000000001001101011100001\n0111110100100 000000000000000000000000000100000000000000000000001000011100100\n0111110110100 000000000000000000000000100100001000010000000000001000011000001\n0111110110101 000000000000001000000000011000000000000000000010000000000100000\n0111110100101 000010000000100000001001000000001000010000000000000000000000001\n0111110100110 001000000010000000000010011000000000000000000100000000000000000\n0111110100111 100000000000000000000000000000000000000000000000000000000000000\n0111110110110 000010000000100000001001000000001000010000000000000000000000001\n0111110110111 001000000010000000000010011000000000000000000100000000000000000\n0111110111000 100000000000000000000000000000000000000000000000000000000000000\n01111001x0010 000000000000000000000000000000000000000000000001000101001100000\n01111001x0011 000000000000100010000001000000001000010000000001001101011100001\n0111100100100 000000000000000000000000000100000000000000000000001000011100100\n0111100110100 000000000000000000000000100100001000010000000000001000011000001\n0111100110101 000000000000001000000000011000000000000000000010000000000100000\n0111100100101 000010000000100000001001000000001000010000000000000000000000001\n0111100100110 001000000010000000000010011000000000000000000100000000000000000\n0111100100111 100000000000000000000000000000000000000000000000000000000000000\n0111100110110 000010000000100000001001000000001000010000000000000000000000001\n0111100110111 001000000010000000000010011000000000000000000100000000000000000\n0111100111000 100000000000000000000000000000000000000000000000000000000000000\n0000000000010 000000000000000000000000100000001001001001000000000000001000000\n0000000000011 000000000000000000000000011000000000000000000010100000000100000\n0000000000100 010000000000000000000001000000001000010100000000000000000000000\n0000000000101 000000000000000000000000011100000000000010000000000010001000000\n0000000000110 010000000000000000000001000000001000010100000000000000000000000\n0000000000111 000000000000000100000000011100000000000010000000000000001000000\n0000000001000 010000000000000000000001000000001000010100000000000000000000000\n0000000001001 000000000000000000000000011000000000000010000000000000000000000\n0000000001010 000000000000000000000000000000000000000000000000000000100000010\n0000000001011 000000000000000000000000000000000000000000000000010000000000100\n0000000001100 100000000000000000000000000000000000000000000000000000000000000\n1010000000010 000000000000000000000000000000000000000000000001000101001100000\n1010000000011 001000000010000000000000100000001000010000000000001000010000001\n1010000000100 000000000000000001000000011000000000000000000000000000000000000\n1010000000101 100000000000000000000000000000000000000000000000000000000000000\n1010010000010 000000000000000000000000000000000000000000000001000101001100000\n1010010000011 000000000000000000000000000000000000000000000000001000011111010\n1010010000100 001000000010000000000000100000001000010000000000000000000000001\n1010010000101 000000000000000001000000011000000000000000000000000000000000000\n1010010000110 100000000000000000000000000000000000000000000000000000000000000\n1011010000010 000000000000000000000000000000000000000000000001000101001100000\n1011010000011 000000000000000000100001000000001000010000000000001000010111001\n1011010000100 000000000000000000000000000100000000000000000000000000001000000\n1011010000101 001000000010000000000000100000001000010000000000000000000000001\n1011010000110 000000000000000001000000011000000000000000000000000000000000000\n1011010000111 100000000000000000000000000000000000000000000000000000000000000\n1010110000010 000000000000000000000000000000000000000000000001000101001100000\n1010110000011 000000000000000000000000100000001000010000000001001101011100001\n1010110000100 000000000000000000000000000100000000000000000000001000011100100\n1010110000101 001000000010000000000000100000001000010000000000000000000000001\n1010110000110 000000000000000001000000011000000000000000000000000000000000000\n1010110000111 100000000000000000000000000000000000000000000000000000000000000\n10111100x0010 000000000000000000000000000000000000000000000001000101001100000\n10111100x0011 000000000000100000100001000000001000010000000001001101011100001\n1011110000100 000000000000000000000000000100000000000000000000001000011100100\n1011110010100 000000000000000000000000100100001000010000000000001000011000001\n1011110010101 000000000000001000000000011000000000000000000010000000000100000\n1011110000101 001000000010000000000000100000001000010000000000000000000000001\n1011110000110 000000000000000001000000011000000000000000000000000000000000000\n1011110000111 100000000000000000000000000000000000000000000000000000000000000\n1011110010110 001000000010000000000000100000001000010000000000000000000000001\n1011110010111 000000000000000001000000011000000000000000000000000000000000000\n1011110011000 100000000000000000000000000000000000000000000000000000000000000\n1010001000010 000000000000000000000000000000000000000000000001000101001100000\n1010001000011 001000000010000000000000100000001000010000000000001000010000001\n1010001000100 000000000000000000010000011000000000000000000000000000000000000\n1010001000101 100000000000000000000000000000000000000000000000000000000000000\n1010011000010 000000000000000000000000000000000000000000000001000101001100000\n1010011000011 000000000000000000000000000000000000000000000000001000011111010\n1010011000100 001000000010000000000000100000001000010000000000000000000000001\n1010011000101 000000000000000000010000011000000000000000000000000000000000000\n1010011000110 100000000000000000000000000000000000000000000000000000000000000\n1011011000010 000000000000000000000000000000000000000000000001000101001100000\n1011011000011 000000000000000010000001000000001000010000000000001000010111001\n1011011000100 000000000000000000000000000100000000000000000000000000001000000\n1011011000101 001000000010000000000000100000001000010000000000000000000000001\n1011011000110 000000000000000000010000011000000000000000000000000000000000000\n1011011000111 100000000000000000000000000000000000000000000000000000000000000\n1010111000010 000000000000000000000000000000000000000000000001000101001100000\n1010111000011 000000000000000000000000100000001000010000000001001101011100001\n1010111000100 000000000000000000000000000100000000000000000000001000011100100\n1010111000101 001000000010000000000000100000001000010000000000000000000000001\n1010111000110 000000000000000000010000011000000000000000000000000000000000000\n1010111000111 100000000000000000000000000000000000000000000000000000000000000\n10111110x0010 000000000000000000000000000000000000000000000001000101001100000\n10111110x0011 000000000000100010000001000000001000010000000001001101011100001\n1011111000100 000000000000000000000000000100000000000000000000001000011100100\n1011111010100 000000000000000000000000100100001000010000000000001000011000001\n1011111010101 000000000000001000000000011000000000000000000010000000000100000\n1011111000101 001000000010000000000000100000001000010000000000000000000000001\n1011111000110 000000000000000000010000011000000000000000000000000000000000000\n1011111000111 100000000000000000000000000000000000000000000000000000000000000\n1011111010110 001000000010000000000000100000001000010000000000000000000000001\n1011111010111 000000000000000000010000011000000000000000000000000000000000000\n1011111011000 100000000000000000000000000000000000000000000000000000000000000\n1010100100010 000000000000000000000000000000000000000000000001000101001100000\n1010100100011 001000000010000000000000100000001000010000000000001000010000001\n1010100100100 000000000000000000000010011000000000000000000000000000000000000\n1010100100101 100000000000000000000000000000000000000000000000000000000000000\n1010010100010 000000000000000000000000000000000000000000000001000101001100000\n1010010100011 000000000000000000000000000000000000000000000000001000011111010\n1010010100100 001000000010000000000000100000001000010000000000000000000000001\n1010010100101 000000000000000000000010011000000000000000000000000000000000000\n1010010100110 100000000000000000000000000000000000000000000000000000000000000\n1011010100010 000000000000000000000000000000000000000000000001000101001100000\n1011010100011 000000000000000000100001000000001000010000000000001000010111001\n1011010100100 000000000000000000000000000100000000000000000000000000001000000\n1011010100101 001000000010000000000000100000001000010000000000000000000000001\n1011010100110 000000000000000000000010011000000000000000000000000000000000000\n1011010100111 100000000000000000000000000000000000000000000000000000000000000\n1010110100010 000000000000000000000000000000000000000000000001000101001100000\n1010110100011 000000000000000000000000100000001000010000000001001101011100001\n1010110100100 000000000000000000000000000100000000000000000000001000011100100\n1010110100101 001000000010000000000000100000001000010000000000000000000000001\n1010110100110 000000000000000000000010011000000000000000000000000000000000000\n1010110100111 100000000000000000000000000000000000000000000000000000000000000\n10111101x0010 000000000000000000000000000000000000000000000001000101001100000\n10111101x0011 000000000000100000100001000000001000010000000001001101011100001\n1011110100100 000000000000000000000000000100000000000000000000001000011100100\n1011110110100 000000000000000000000000100100001000010000000000001000011000001\n1011110110101 000000000000001000000000011000000000000000000010000000000100000\n1011110100101 001000000010000000000000100000001000010000000000000000000000001\n1011110100110 000000000000000000000010011000000000000000000000000000000000000\n1011110100111 100000000000000000000000000000000000000000000000000000000000000\n1011110110110 001000000010000000000000100000001000010000000000000000000000001\n1011110110111 000000000000000000000010011000000000000000000000000000000000000\n1011110111000 100000000000000000000000000000000000000000000000000000000000000\n10111001x0010 000000000000000000000000000000000000000000000001000101001100000\n10111001x0011 000000000000100010000001000000001000010000000001001101011100001\n1011100100100 000000000000000000000000000100000000000000000000001000011100100\n1011100110100 000000000000000000000000100100001000010000000000001000011000001\n1011100110101 000000000000001000000000011000000000000000000010000000000100000\n1011100100101 001000000010000000000000100000001000010000000000000000000000001\n1011100100110 000000000000000000000010011000000000000000000000000000000000000\n1011100100111 100000000000000000000000000000000000000000000000000000000000000\n1011100110110 001000000010000000000000100000001000010000000000000000000000001\n1011100110111 000000000000000000000010011000000000000000000000000000000000000\n1011100111000 100000000000000000000000000000000000000000000000000000000000000\n0011100000010 000000000000010000000000000000000000000000000001000101001100000\n0011100000011 000000000000000000000000000000000000000000000000001000010000000\n0011100000100 100000000000000000000000000000000000000000000000000000000000000\n1111100000010 000000100000000000000000000000000000000000000001000101001100000\n1111100000011 000000000000000000000000000000000000000000000000001000010000000\n1111100000100 100000000000000000000000000000000000000000000000000000000000000\n0111100000010 000000001000000000000000000000000000000000000001000101001100000\n0111100000011 000000000000000000000000000000000000000000000000001000010000000\n0111100000100 100000000000000000000000000000000000000000000000000000000000000\n1000010100010 000000000000000000000000000000000000000000000001000101001100000\n1000010100011 000000000000000000000100000000000000000000000000001000011111010\n1000010100100 010000000000000000000000000000000000000000000000000000000000000\n1000010100101 100000000000000000000000000000000000000000000000000000000000000\n1001010100010 000000000000000000000000000000000000000000000001000101001100000\n1001010100011 000000000000000000100001000000001000010000000000001000010111001\n1001010100100 000000000000000000000100000100000000000000000000000000001000000\n1001010100101 010000000000000000000000000000000000000000000000000000000000000\n1001010100110 100000000000000000000000000000000000000000000000000000000000000\n1000110100010 000000000000000000000000000000000000000000000001000101001100000\n1000110100011 000000000000000000000000100000001000010000000001001101011100001\n1000110100100 000000000000000000000100000100000000000000000000001000011100100\n1000110100101 010000000000000000000000000000000000000000000000000000000000000\n1000110100110 100000000000000000000000000000000000000000000000000000000000000\n10011101x0010 000000000000000000000000000000000000000000000001000101001100000\n10011101x0011 000000000000100000100001000000001000010000000001001101011100001\n1001110100100 000000000000000000000100000100000000000000000000001000011100100\n1001110110100 000000000000000000000000100100001000010000000000001000011000001\n1001110110101 000000000000001000000000011000000000000000000010000000000100000\n1001110100101 010000000000000000000000000000000000000000000000000000000000000\n1001110100110 100000000000000000000000000000000000000000000000000000000000000\n1001110110110 010000000000000000000000000000000000000000000000000000000000000\n1001110110111 100000000000000000000000000000000000000000000000000000000000000\n10011001x0010 000000000000000000000000000000000000000000000001000101001100000\n10011001x0011 000000000000100010000001000000001000010000000001001101011100001\n1001100100100 000000000000000000000100000100000000000000000000001000011100100\n1001100110100 000000000000000000000000100100001000010000000000001000011000001\n1001100110101 000000000000001000000000011000000000000000000010000000000100000\n1001100100101 010000000000000000000000000000000000000000000000000000000000000\n1001100100110 100000000000000000000000000000000000000000000000000000000000000\n1001100110110 010000000000000000000000000000000000000000000000000000000000000\n1001100110111 100000000000000000000000000000000000000000000000000000000000000\n1000011000010 000000000000000000000000000000000000000000000001000101001100000\n1000011000011 000000000000000000100000000000000000000000000100001000011111010\n1000011000100 010000000000000000000000000000000000000000000000000000000000000\n1000011000101 100000000000000000000000000000000000000000000000000000000000000\n1001011000010 000000000000000000000000000000000000000000000001000101001100000\n1001011000011 000000000000000010000001000000001000010000000000001000010111001\n1001011000100 000000000000000000100000000100000000000000000100000000001000000\n1001011000101 010000000000000000000000000000000000000000000000000000000000000\n1001011000110 100000000000000000000000000000000000000000000000000000000000000\n1000111000010 000000000000000000000000000000000000000000000001000101001100000\n1000111000011 000000000000000000000000100000001000010000000001001101011100001\n1000111000100 000000000000000000100000000100000000000000000100001000011100100\n1000111000101 010000000000000000000000000000000000000000000000000000000000000\n1000111000110 100000000000000000000000000000000000000000000000000000000000000\n1000010000010 000000000000000000000000000000000000000000000001000101001100000\n1000010000011 000000000000000010000000000000000000000000000100001000011111010\n1000010000100 010000000000000000000000000000000000000000000000000000000000000\n1000010000101 100000000000000000000000000000000000000000000000000000000000000\n1001010000010 000000000000000000000000000000000000000000000001000101001100000\n1001010000011 000000000000000000100001000000001000010000000000001000010111001\n1001010000100 000000000000000010000000000100000000000000000100000000001000000\n1001010000101 010000000000000000000000000000000000000000000000000000000000000\n1001010000110 100000000000000000000000000000000000000000000000000000000000000\n1000110000010 000000000000000000000000000000000000000000000001000101001100000\n1000110000011 000000000000000000000000100000001000010000000001001101011100001\n1000110000100 000000000000000010000000000100000000000000000100001000011100100\n1000110000101 010000000000000000000000000000000000000000000000000000000000000\n1000110000110 100000000000000000000000000000000000000000000000000000000000000\n1010101000010 000000000000000000000000000000000000000000000001000101001100000\n1010101000011 001000000010000000011000000000000000000000000100001000010000000\n1010101000100 100000000000000000000000000000000000000000000000000000000000000\n1010100000010 000000000000000000000000000000000000000000000001000101001100000\n1010100000011 001000000010000001001000000000000000000000000100001000010000000\n1010100000100 100000000000000000000000000000000000000000000000000000000000000\n1011101000010 000000000000000000000000000000000000000000000001000101001100000\n1011101000011 001000000010000000100000000000000000000010000100001000010000000\n1011101000100 100000000000000000000000000000000000000000000000000000000000000\n1000101000010 000000000000000000000000000000000000000000000001000101001100000\n1000101000011 001000000010000000100010000000000000000000000100001000010000000\n1000101000100 100000000000000000000000000000000000000000000000000000000000000\n1001101000010 000000000000000000000000000000000000000000000001000101001100000\n1001101000011 000000000000000000100000000000000000000010000000001000010000000\n1001101000100 100000000000000000000000000000000000000000000000000000000000000\n1001100000010 000000000000000000000000000000000000000000000001000101001100000\n1001100000011 001000000010000010000010000000000000000000000100001000010000000\n1001100000100 100000000000000000000000000000000000000000000000000000000000000")) DecodePLA (
    .in(counter_1_q), .out(DecodePLA_out));
  PLA #(.in_width(4), .out_width(63), .\table ("0000 000000000000000000000000000000000000000000000000000000000000000\n0001 000000000000000000000000100000001000010000000000000000100000010\n0010 000000000000000000000000011000000000000010000000010000000000100\n0100 100000000000000000000000000000000000000000000000000000000000000")) ResetPLA (
    .in(counter_1_q[3:0]), .out(ResetPLA_out));
  and and_2 (RSTLB_ADB, RST_q, decoder_1_out0);
  and and_3 (RSTHB_ADB, RST_q, decoder_1_out1);
  not not_2 (CL2, CLCK);
  or or_2 (or_2_out, RST, RST_CYCLE);
  Counter #(.max('hf), .width(4)) counter_1 (
    .clr(or_2_out), .up(1'b1), .count(1'b1), .clk(CL2), .Q(counter_1_q[3:0]));  // open: load, D, carry
  PLA #(.in_width(8), .out_width(3), .\table ("01101001 000\n01100101 000\n01110101 000\n01101101 000\n01111101 001\n01111001 001\n00000000 000\n10100000 000\n10100100 000\n10110100 000\n10101100 000\n10111100 001\n10100010 000\n10100110 000\n10110110 000\n10101110 000\n10111110 001\n10101001 000\n10100101 000\n10110101 000\n10101101 000\n10111101 001\n10111001 001\n00111000 000\n11111000 000\n01111000 000\n10000101 000\n10010101 000\n10001101 000\n10011101 001\n10011001 001\n10000110 000\n10010110 000\n10001110 000\n10000100 000\n10010100 000\n10001100 000\n10101010 000\n10101000 000\n10111010 000\n10001010 000\n10011010 000\n10011000 000")) FlagSelect (
    .in(counter_1_q[12:5]), .out(FlagSelect_out));
  assign not_3_out = ~bit_extender_2_out;  // NOT_Gate not_3, 63 bits wide
  assign bit_extender_2_out = {{62{RST_q}}, RST_q};  // Bit_Extender bit_extender_2
  assign and_4_out = bit_extender_2_out & ResetPLA_out;  // AND_Gate and_4, 63 bits wide
  and and_5 (BRK, decoder_2_out2, IRQPLA_out[0]);
  and and_6 (BRKLB_ADB, decoder_2_out9, IRQPLA_out[0]);
  and and_7 (BRKHB_ADB, IRQPLA_out[0], decoder_2_out10);
  assign and_8_out = DecodePLA_out & not_3_out;  // AND_Gate and_8, 63 bits wide
  assign {RST_CYCLE, RW, DB7_N, I_V, AVR_V, DB6_V, IR5_D, DB3_D, IR5_I, DB2_I, DBZ_Z, DB1_Z, ACR_C, IR5_C, DB0_C, P_DB, Y_SB, SB_Y, X_SB, SB_X, AC_SB, AC_DB, SB_AC, SB_ADD, O_ADD, ADD_SB7, ADD_SB06, ADD_ADL, SRS, ORS, EORS, ANDS, SUMS, DSA, DAA, I_ADDC, ADL_ADD, DB_ADD, DBx_ADD, S_SB, SB_S, S_ADL, O_ADL2, O_ADL1, O_ADL0, SB_DB, SB_ADH, PCH_ADH, PCH_DB, ADH_PCH, PCH_PCH, PCL_ADL, PCL_DB, I_PC, ADL_PCL, PCL_PCL, ADL_ABL, ADH_ABH, O_ADH17, O_ADH0, DL_ADH, DL_ADL, DL_DB} = and_8_out | and_4_out;  // OR_Gate or_3, 63 bits wide
  Register PD (.D(DATA_IN), .en(CL2), .clk(CL2), .Q(PD_q), .clr(RST));
  Pull_Resistor pull_resistor_2 (.node(pull_resistor_2_node));
  Register DOR (.D(controlled_buffer_2_out), .en(CLCK), .clk(CLCK), .Q(DOR_q), .clr(RST));
  Decoder #(.enable("false"), .select(4)) decoder_2 (
    .out1(decoder_2_out1), .out2(decoder_2_out2), .out9(decoder_2_out9), .out10(decoder_2_out10),
    .sel(counter_1_q[3:0]));  // open: out0, out3, out4, out5, out6, out7, out8, out11, out12, out13, out14, out15
  assign DATA_IN = RW ? DOR_q : 8'bz;  // Controlled_Buffer controlled_buffer_1
  assign controlled_buffer_2_out = DL_DB ? DL_q : 8'bz;  // Controlled_Buffer controlled_buffer_2
  Pull_Resistor #(.pull(1)) pull_resistor_3 (.node(controlled_buffer_2_out));
  BitSelector bitselector_1 (.in(counter_1_q[12:5]), .out(bitselector_1_out), .sel(3'b101));
  assign not_4_out = ~controlled_buffer_2_out;  // NOT_Gate not_4, 8 bits wide
  assign controlled_buffer_3_out = DBx_ADD ? not_4_out : 8'bz;  // Controlled_Buffer controlled_buffer_3
  Register AI (.D(controlled_buffer_13_out), .en(or_7_out), .clk(CLCK), .Q(AI_q), .clr(RST));
  Priority_Encoder #(.select(2)) priority_encoder_1 (
    .in0(1'b1), .in1(DB2_I), .in2(IR5_I), .in3(1'b0), .out(priority_encoder_1_out));
  Multiplexer multiplexer_2 (.in0(B), .in1(1'b1), .out(multiplexer_3_out[4]), .sel(BRK));
  or or_4 (or_4_out, ADL_PCL, PCL_PCL);
  assign controlled_buffer_2_out = PCL_DB ? PCL_q : 8'bz;  // Controlled_Buffer controlled_buffer_4
  assign controlled_buffer_3_out = DB_ADD ? controlled_buffer_2_out : 8'bz;  // Controlled_Buffer controlled_buffer_5
  or or_5 (or_5_out, C, I_ADDC);
  Multiplexer #(.select(2)) multiplexer_3 (
    .in0(C), .in1(controlled_buffer_2_out[0]), .in2(bitselector_1_out), .in3(ACR),
    .out(multiplexer_3_out[0]), .sel(priority_encoder_2_out));
  Priority_Encoder #(.select(2)) priority_encoder_2 (
    .in0(1'b1), .in1(DB0_C), .in2(IR5_C), .in3(ACR_C), .out(priority_encoder_2_out));
  Multiplexer #(.select(2)) multiplexer_4 (
    .in0(I), .in1(controlled_buffer_2_out[2]), .in2(bitselector_1_out), .in3(1'b0),
    .out(multiplexer_3_out[2]), .sel(priority_encoder_1_out));
  Priority_Encoder #(.select(2)) priority_encoder_3 (
    .in0(1'b1), .in1(DB3_D), .in2(IR5_D), .in3(1'b0), .out(priority_encoder_3_out));
  Priority_Encoder #(.select(2)) priority_encoder_4 (
    .in0(1'b1), .in1(DB6_V), .in2(AVR_V), .in3(I_V), .out(priority_encoder_4_out));
  Multiplexer multiplexer_5 (.in0(N), .in1(controlled_buffer_2_out[7]), .out(multiplexer_3_out[7]), .sel(DB7_N));
  assign controlled_buffer_6_out = ADL_PCL ? controlled_buffer_9_out : 8'bz;  // Controlled_Buffer controlled_buffer_6
  assign controlled_buffer_6_out = PCL_PCL ? PCL_q : 8'bz;  // Controlled_Buffer controlled_buffer_7
  or or_6 (or_6_out, DBx_ADD, DB_ADD, ADL_ADD);
  Register BI (.D(controlled_buffer_3_out), .en(or_6_out), .clk(CLCK), .Q(BI_q), .clr(RST));
  Multiplexer #(.select(2)) multiplexer_6 (
    .in0(Z), .in1(controlled_buffer_2_out[1]), .in2(not_5_out), .in3(1'b0), .out(multiplexer_3_out[1]),
    .sel(priority_encoder_5_out));
  Priority_Encoder #(.select(2)) priority_encoder_5 (
    .in0(1'b1), .in1(DB1_Z), .in2(DBZ_Z), .in3(1'b0), .out(priority_encoder_5_out));
  Multiplexer #(.select(2)) multiplexer_7 (
    .in0(D), .in1(controlled_buffer_2_out[3]), .in2(bitselector_1_out), .in3(1'b0),
    .out(multiplexer_3_out[3]), .sel(priority_encoder_3_out));
  Multiplexer #(.select(2)) multiplexer_8 (
    .in0(V), .in1(controlled_buffer_2_out[6]), .in2(AVR), .in3(1'b1), .out(multiplexer_3_out[6]),
    .sel(priority_encoder_4_out));
  Register PCLS (.D(controlled_buffer_6_out), .en(or_4_out), .clk(CLCK), .Q(PCLS_q), .clr(RST));
  assign bit_extender_3_out = {{7{1'b0}}, I_PC};  // Bit_Extender bit_extender_3
  Adder adder_1 (.a(PCLS_q), .b(bit_extender_3_out), .out(adder_1_out), .cout(adder_1_cout));  // open: cin
  Register PCL (.D(adder_1_out), .en(CL2), .clk(CL2), .Q(PCL_q), .clr(RST));
  assign controlled_buffer_3_out = ADL_ADD ? controlled_buffer_9_out : 8'bz;  // Controlled_Buffer controlled_buffer_8
  ALU8b ALU8b_1 (
    .Input_1(or_5_out), .Input_2(DAA), .Input_bus_1(BI_q), .Input_3(SUMS), .Input_4(ANDS), .Input_5(EORS),
    .Input_6(ORS), .in_8(SRS), .in_9(AI_q), .Output_bus_1(ALU8b_1_output_bus_1), .Output_1(HC),
    .Output_2(AVR), .out_13(ACR));
  Register DL (.D(DATA_IN), .en(CL2), .clk(CL2), .Q(DL_q), .clr(RST));
  assign controlled_buffer_9_out = PCL_ADL ? PCL_q : 8'bz;  // Controlled_Buffer controlled_buffer_9
  assign controlled_buffer_9_out[0] = O_ADL0 ? 1'b0 : 1'bz;  // Controlled_Buffer controlled_buffer_10
  assign controlled_buffer_9_out[1] = O_ADL1 ? 1'b0 : 1'bz;  // Controlled_Buffer controlled_buffer_11
  assign controlled_buffer_9_out[2] = O_ADL2 ? 1'b0 : 1'bz;  // Controlled_Buffer controlled_buffer_12
  assign controlled_buffer_13_out = O_ADD ? {8{1'b0}} : 8'bz;  // Controlled_Buffer controlled_buffer_13
  Register P (
    .D({multiplexer_3_out[7:6], 1'b1, multiplexer_3_out[4:0]}), .en(or_8_out), .clk(CLCK),
    .Q({N, V, P_q[5], B, D, I, Z, C}), .clr(RST));
  assign controlled_buffer_9_out = DL_ADL ? DL_q : 8'bz;  // Controlled_Buffer controlled_buffer_14
  Pull_Resistor #(.pull(1)) pull_resistor_4 (.node(controlled_buffer_9_out));
  assign controlled_buffer_9_out = ADD_ADL ? ADD_q : 8'bz;  // Controlled_Buffer controlled_buffer_15
  Register ADD (.D(ALU8b_1_output_bus_1), .en(CL2), .clk(CL2), .Q(ADD_q), .clr(RST));
  or or_7 (or_7_out, O_ADD, SB_ADD);
  assign controlled_buffer_2_out = P_DB ? {N, V, P_q[5], B, D, I, Z, C} : 8'bz;  // Controlled_Buffer controlled_buffer_16
  // NoConnect on P_q[5]
  assign controlled_buffer_2_out = PCH_DB ? PCH_q : 8'bz;  // Controlled_Buffer controlled_buffer_17
  assign controlled_buffer_9_out = S_ADL ? S_q : 8'bz;  // Controlled_Buffer controlled_buffer_18
  assign controlled_buffer_13_out = SB_ADD ? {controlled_buffer_21_out[7], controlled_buffer_20_out} : 8'bz;  // Controlled_Buffer controlled_buffer_19
  or or_8 (or_8_out, DB0_C, IR5_C, ACR_C, DB2_I, IR5_I, DB1_Z, DBZ_Z, DB3_D, IR5_D, BRK, DB6_V, AVR_V, I_V, DB7_N);
  or or_9 (or_9_out, ADH_PCH, PCH_PCH);
  assign controlled_buffer_20_out = ADD_SB06 ? ADD_q[6:0] : 7'bz;  // Controlled_Buffer controlled_buffer_20
  assign controlled_buffer_21_out[7] = ADD_SB7 ? ADD_q[7] : 1'bz;  // Controlled_Buffer controlled_buffer_21
  or or_10 (or_10_out, controlled_buffer_2_out[7], controlled_buffer_2_out[6], controlled_buffer_2_out[5], controlled_buffer_2_out[4], controlled_buffer_2_out[3], controlled_buffer_2_out[2], controlled_buffer_2_out[1], controlled_buffer_2_out[0]);
  not not_5 (not_5_out, or_10_out);
  assign controlled_buffer_22_out = ADH_PCH ? controlled_buffer_27_out : 8'bz;  // Controlled_Buffer controlled_buffer_22
  assign controlled_buffer_22_out = PCH_PCH ? PCH_q : 8'bz;  // Controlled_Buffer controlled_buffer_23
  assign controlled_buffer_2_out = SB_DB ? {controlled_buffer_21_out[7], controlled_buffer_20_out} : 8'bz;  // Controlled_Buffer controlled_buffer_24
  Register S (.D({controlled_buffer_21_out[7], controlled_buffer_20_out}), .en(SB_S), .clk(CLCK), .Q(S_q), .clr(RST));
  Register AC (
    .D({controlled_buffer_21_out[7], controlled_buffer_20_out}), .en(SB_AC), .clk(CLCK), .Q(AC_q), .clr(RST));
  assign controlled_buffer_2_out = AC_DB ? AC_q : 8'bz;  // Controlled_Buffer controlled_buffer_25
  Register PCHS (.D(controlled_buffer_22_out), .en(or_9_out), .clk(CLCK), .Q(PCHS_q), .clr(RST));
  Adder adder_2 (.a(PCHS_q), .b({8{1'b0}}), .out(adder_2_out), .cin(adder_1_cout));  // open: cout
  Register PCH (.D(adder_2_out), .en(CL2), .clk(CL2), .Q(PCH_q), .clr(RST));
  assign {controlled_buffer_21_out[7], controlled_buffer_20_out} = AC_SB ? AC_q : 8'bz;  // Controlled_Buffer controlled_buffer_26
  assign controlled_buffer_27_out = PCH_ADH ? PCH_q : 8'bz;  // Controlled_Buffer controlled_buffer_27
  assign {controlled_buffer_21_out[7], controlled_buffer_20_out} = S_SB ? S_q : 8'bz;  // Controlled_Buffer controlled_buffer_28
  assign controlled_buffer_27_out = DL_ADH ? DL_q : 8'bz;  // Controlled_Buffer controlled_buffer_29
  Pull_Resistor #(.pull(1)) pull_resistor_5 (.node(controlled_buffer_27_out));
  assign controlled_buffer_27_out = SB_ADH ? {controlled_buffer_21_out[7], controlled_buffer_20_out} : 8'bz;  // Controlled_Buffer controlled_buffer_30
  Pull_Resistor #(.pull(1)) pull_resistor_6 (.node({controlled_buffer_21_out[7], controlled_buffer_20_out}));
  Register ABH (.D(controlled_buffer_27_out), .en(ADH_ABH), .clk(CLCK), .Q(ABH_q), .clr(RST));
  Register ABL (.D(controlled_buffer_9_out), .en(ADL_ABL), .clk(CLCK), .Q(ABL_q), .clr(RST));
  Register X (.D({controlled_buffer_21_out[7], controlled_buffer_20_out}), .en(SB_X), .clk(CLCK), .Q(X_q), .clr(RST));
  assign {controlled_buffer_21_out[7], controlled_buffer_20_out} = X_SB ? X_q : 8'bz;  // Controlled_Buffer controlled_buffer_31
  Register Y (.D({controlled_buffer_21_out[7], controlled_buffer_20_out}), .en(SB_Y), .clk(CLCK), .Q(Y_q), .clr(RST));
  assign {controlled_buffer_21_out[7], controlled_buffer_20_out} = Y_SB ? Y_q : 8'bz;  // Controlled_Buffer controlled_buffer_32
  assign controlled_buffer_27_out[0] = O_ADH0 ? 1'b0 : 1'bz;  // Controlled_Buffer controlled_buffer_33
  assign controlled_buffer_27_out[7:1] = O_ADH17 ? {7{1'b0}} : 7'bz;  // Controlled_Buffer controlled_buffer_34
  PLA #(.in_width(3), .out_width(16), .\table ("010 1111111111111100\n011 1111111111111101\n100 1111111111111110\n101 1111111111111111")) Vectors (
    .in(or_11_out), .out(Vectors_out));
  Multiplexer #(.width(16)) multiplexer_9 (.in0({ABH_q, ABL_q}), .in1(Vectors_out), .out(ADDR), .sel(or_12_out));
  or or_11 (or_11_out[0], BRKHB_ADB, RSTHB_ADB);
  or or_12 (or_12_out, RSTLB_ADB, RSTHB_ADB, BRKLB_ADB, BRKHB_ADB);
  or or_13 (or_11_out[1], RSTLB_ADB, RSTHB_ADB);
  or or_14 (or_11_out[2], BRKLB_ADB, BRKHB_ADB);

  assign DATA_OUT = DATA_IN;

  // Other names for the same wires on the sheet: CL1 = CLCK
endmodule
